# Fritzing sketch head_circuit (saved by Fritzing 0.9.6b)

parts:
  Mod1 = Raspberry Pi 4B
  LED1 = LEDs [package=led10mm]
  LED2 = LEDs [package=led10mm]
  U1 = TCM8240MD [package=tcm8240md]  # not connected
  U2 = TRANSCHIPTC5747 [package=camera_sfv24r-2st_2]  # not connected
  U3 = TCM8240MD [package=tcm8240md]  # not connected
  J2 = Basic Servo
  VCC1 = 4 x AAA Battery Mount
  R1 = Resistor [tolerance=±5% resistance=220 package="0603 [SMD]"]
  R2 = Resistor [tolerance=±5% resistance=220 package="0603 [SMD]"]
  J1 = Basic Servo

nets:
  GND: Mod1.GND, J2.gnd, VCC1.-, R1.Pin_1, R2.Pin_0, J1.gnd
  N1: Mod1.GPIO17, LED2.C
  N2: Mod1.GPIO26, LED1.C

notes:
  stero camera to USB
  time of flight 2 pi camera input
